// Logisim project EE21B001_DSCLOCKDESIGN_24HRS.circ as structural Verilog: 2 circuits, main circuit main
module main (
);

  wire and_1_out, and_2_out, and_3_out, and_4_out, and_5_out, and_6_out, and_7_out, and_8_out, and_9_out,
       and_10_out, and_11_out, and_12_out, and_13_out, and_14_out, and_15_out, and_16_out, and_17_out,
       and_18_out, and_19_out, and_20_out, and_21_out, and_22_out, and_23_out, and_24_out, and_25_out,
       and_26_out, and_27_out, clock_1_out, decoder_1_a0, decoder_1_a1, decoder_1_a2, decoder_1_a3,
       decoder_1_a4, decoder_1_a5, decoder_1_a6, decoder_2_a0, decoder_2_a1, decoder_2_a2, decoder_2_a3,
       decoder_2_a4, decoder_2_a5, decoder_2_a6, decoder_3_a0, decoder_3_a1, decoder_3_a2, decoder_3_a3,
       decoder_3_a4, decoder_3_a5, decoder_3_a6, decoder_4_a0, decoder_4_a1, decoder_4_a2, decoder_4_a3,
       decoder_4_a4, decoder_4_a5, decoder_4_a6, decoder_5_a0, decoder_5_a1, decoder_5_a2, decoder_5_a3,
       decoder_5_a4, decoder_5_a5, decoder_5_a6, decoder_6_a0, decoder_6_a1, decoder_6_a2, decoder_6_a3,
       decoder_6_a4, decoder_6_a5, decoder_6_a6, or_1_out, t_ff_1_q, t_ff_2_q, t_ff_3_q, t_ff_4_q, t_ff_5_q,
       t_ff_6_q, t_ff_7_q, t_ff_8_q, t_ff_9_q, t_ff_10_q, t_ff_11_q, t_ff_12_q, t_ff_13_q, t_ff_14_q,
       t_ff_15_q, t_ff_16_q, t_ff_17_q, t_ff_18_q, t_ff_19_q, t_ff_20_q, t_ff_21_q, t_ff_22_q, t_ff_23_q,
       t_ff_24_q;

  T_Flip_Flop t_ff_1 (
    .clk(clock_1_out), .T(1'b1), .Q(t_ff_1_q), .reset(and_10_out), .en(and_1_out));  // open: Qn, preset
  and and_1 (and_1_out, and_4_out, and_2_out);
  T_Flip_Flop t_ff_2 (
    .clk(clock_1_out), .T(t_ff_1_q), .Q(t_ff_2_q), .reset(and_10_out), .en(and_1_out));  // open: Qn, preset
  and and_2 (and_2_out, t_ff_4_q, t_ff_10_q);
  and and_3 (and_3_out, t_ff_2_q, t_ff_1_q);
  and and_4 (and_4_out, and_7_out, and_5_out);
  and and_5 (and_5_out, t_ff_7_q, t_ff_11_q);
  T_Flip_Flop t_ff_3 (
    .clk(clock_1_out), .T(and_3_out), .Q(t_ff_3_q), .reset(and_10_out), .en(and_1_out));  // open: Qn, preset
  and and_6 (and_6_out, t_ff_3_q, and_3_out);
  T_Flip_Flop t_ff_4 (.clk(clock_1_out), .T(1'b1), .Q(t_ff_4_q), .reset(or_1_out), .en(and_4_out));  // open: Qn, preset
  T_Flip_Flop t_ff_5 (
    .clk(clock_1_out), .T(and_6_out), .Q(t_ff_5_q), .reset(and_10_out), .en(and_1_out));  // open: Qn, preset
  T_Flip_Flop t_ff_6 (
    .clk(clock_1_out), .T(t_ff_4_q), .Q(t_ff_6_q), .reset(or_1_out), .en(and_4_out));  // open: Qn, preset
  T_Flip_Flop t_ff_7 (
    .clk(clock_1_out), .T(1'b1), .Q(t_ff_7_q), .reset(and_16_out), .en(and_7_out));  // open: Qn, preset
  and and_7 (and_7_out, and_13_out, and_9_out);
  T_Flip_Flop t_ff_8 (
    .clk(clock_1_out), .T(and_8_out), .Q(t_ff_8_q), .reset(or_1_out), .en(and_4_out));  // open: Qn, preset
  and and_8 (and_8_out, t_ff_6_q, t_ff_4_q);
  T_Flip_Flop t_ff_9 (
    .clk(clock_1_out), .T(t_ff_7_q), .Q(t_ff_9_q), .reset(and_16_out), .en(and_7_out));  // open: Qn, preset
  and and_9 (and_9_out, t_ff_12_q, t_ff_19_q);
  _7_Segment_Display u_7_segment_display_1 (
    .g(decoder_1_a0), .f(decoder_1_a1), .a(decoder_1_a2), .b(decoder_1_a3), .e(decoder_1_a4),
    .d(decoder_1_a5), .c(decoder_1_a6));  // open: dp
  decoder decoder_1 (
    .a(t_ff_5_q), .b(t_ff_3_q), .c(t_ff_2_q), .d(t_ff_1_q), .a0(decoder_1_a0), .a1(decoder_1_a1),
    .a2(decoder_1_a2), .a3(decoder_1_a3), .a4(decoder_1_a4), .a5(decoder_1_a5), .a6(decoder_1_a6));
  and and_10 (and_10_out, t_ff_2_q, t_ff_8_q);
  and and_11 (and_11_out, t_ff_8_q, and_8_out);
  or or_1 (or_1_out, and_14_out, and_10_out);
  and and_12 (and_12_out, t_ff_9_q, t_ff_7_q);
  and and_13 (and_13_out, and_18_out, and_24_out);
  T_Flip_Flop t_ff_10 (
    .clk(clock_1_out), .T(and_11_out), .Q(t_ff_10_q), .reset(or_1_out), .en(and_4_out));  // open: Qn, preset
  and and_14 (and_14_out, t_ff_6_q, t_ff_10_q);
  T_Flip_Flop t_ff_11 (
    .clk(clock_1_out), .T(and_12_out), .Q(t_ff_11_q), .reset(and_16_out), .en(and_7_out));  // open: Qn, preset
  T_Flip_Flop t_ff_12 (
    .clk(clock_1_out), .T(1'b1), .Q(t_ff_12_q), .reset(and_22_out), .en(and_13_out));  // open: Qn, preset
  T_Flip_Flop t_ff_13 (
    .clk(clock_1_out), .T(and_15_out), .Q(t_ff_13_q), .reset(and_16_out), .en(and_7_out));  // open: Qn, preset
  and and_15 (and_15_out, t_ff_11_q, and_12_out);
  T_Flip_Flop t_ff_14 (
    .clk(clock_1_out), .T(1'b1), .Q(t_ff_14_q), .reset(and_23_out), .en(and_24_out));  // open: Qn, preset
  _7_Segment_Display u_7_segment_display_2 (
    .g(decoder_2_a0), .f(decoder_2_a1), .a(decoder_2_a2), .b(decoder_2_a3), .e(decoder_2_a4),
    .d(decoder_2_a5), .c(decoder_2_a6));  // open: dp
  decoder decoder_2 (
    .a(t_ff_10_q), .b(t_ff_8_q), .c(t_ff_6_q), .d(t_ff_4_q), .a0(decoder_2_a0), .a1(decoder_2_a1),
    .a2(decoder_2_a2), .a3(decoder_2_a3), .a4(decoder_2_a4), .a5(decoder_2_a5), .a6(decoder_2_a6));
  and and_16 (and_16_out, t_ff_9_q, t_ff_11_q);
  T_Flip_Flop t_ff_15 (
    .clk(clock_1_out), .T(t_ff_12_q), .Q(t_ff_15_q), .reset(and_22_out), .en(and_13_out));  // open: Qn, preset
  and and_17 (and_17_out, t_ff_15_q, t_ff_12_q);
  and and_18 (and_18_out, t_ff_14_q, t_ff_18_q);
  T_Flip_Flop t_ff_16 (
    .clk(clock_1_out), .T(and_17_out), .Q(t_ff_16_q), .reset(and_22_out), .en(and_13_out));  // open: Qn, preset
  T_Flip_Flop t_ff_17 (
    .clk(clock_1_out), .T(t_ff_14_q), .Q(t_ff_17_q), .reset(and_23_out), .en(and_24_out));  // open: Qn, preset
  and and_19 (and_19_out, t_ff_17_q, t_ff_14_q);
  LED led_1 (.in(1'b1));
  LED led_2 (.in(1'b1));
  decoder decoder_3 (
    .a(t_ff_13_q), .b(t_ff_11_q), .c(t_ff_9_q), .d(t_ff_7_q), .a0(decoder_3_a0), .a1(decoder_3_a1),
    .a2(decoder_3_a2), .a3(decoder_3_a3), .a4(decoder_3_a4), .a5(decoder_3_a5), .a6(decoder_3_a6));
  and and_20 (and_20_out, t_ff_16_q, and_17_out);
  T_Flip_Flop t_ff_18 (
    .clk(clock_1_out), .T(and_19_out), .Q(t_ff_18_q), .reset(and_23_out), .en(and_24_out));  // open: Qn, preset
  _7_Segment_Display u_7_segment_display_3 (
    .g(decoder_3_a0), .f(decoder_3_a1), .a(decoder_3_a2), .b(decoder_3_a3), .e(decoder_3_a4),
    .d(decoder_3_a5), .c(decoder_3_a6));  // open: dp
  T_Flip_Flop t_ff_19 (
    .clk(clock_1_out), .T(and_20_out), .Q(t_ff_19_q), .reset(and_22_out), .en(and_13_out));  // open: Qn, preset
  T_Flip_Flop t_ff_20 (
    .clk(clock_1_out), .T(and_21_out), .Q(t_ff_20_q), .reset(and_23_out), .en(and_24_out));  // open: Qn, preset
  and and_21 (and_21_out, t_ff_18_q, and_19_out);
  and and_22 (and_22_out, t_ff_15_q, t_ff_19_q);
  and and_23 (and_23_out, t_ff_18_q, t_ff_17_q);
  and and_24 (and_24_out, t_ff_21_q, t_ff_24_q);
  _7_Segment_Display u_7_segment_display_4 (
    .g(decoder_4_a0), .f(decoder_4_a1), .a(decoder_4_a2), .b(decoder_4_a3), .e(decoder_4_a4),
    .d(decoder_4_a5), .c(decoder_4_a6));  // open: dp
  decoder decoder_4 (
    .a(t_ff_19_q), .b(t_ff_16_q), .c(t_ff_15_q), .d(t_ff_12_q), .a0(decoder_4_a0), .a1(decoder_4_a1),
    .a2(decoder_4_a2), .a3(decoder_4_a3), .a4(decoder_4_a4), .a5(decoder_4_a5), .a6(decoder_4_a6));
  T_Flip_Flop t_ff_21 (.clk(clock_1_out), .T(1'b1), .Q(t_ff_21_q), .reset(and_27_out));  // open: Qn, preset, en
  LED led_3 (.in(1'b1));
  LED led_4 (.in(1'b1));
  T_Flip_Flop t_ff_22 (.clk(clock_1_out), .T(t_ff_21_q), .Q(t_ff_22_q), .reset(and_27_out));  // open: Qn, preset, en
  _7_Segment_Display u_7_segment_display_5 (
    .g(decoder_5_a0), .f(decoder_5_a1), .a(decoder_5_a2), .b(decoder_5_a3), .e(decoder_5_a4),
    .d(decoder_5_a5), .c(decoder_5_a6));  // open: dp
  decoder decoder_5 (
    .a(t_ff_20_q), .b(t_ff_18_q), .c(t_ff_17_q), .d(t_ff_14_q), .a0(decoder_5_a0), .a1(decoder_5_a1),
    .a2(decoder_5_a2), .a3(decoder_5_a3), .a4(decoder_5_a4), .a5(decoder_5_a5), .a6(decoder_5_a6));
  and and_25 (and_25_out, t_ff_22_q, t_ff_21_q);
  T_Flip_Flop t_ff_23 (.clk(clock_1_out), .T(and_25_out), .Q(t_ff_23_q), .reset(and_27_out));  // open: Qn, preset, en
  and and_26 (and_26_out, t_ff_23_q, and_25_out);
  T_Flip_Flop t_ff_24 (.clk(clock_1_out), .T(and_26_out), .Q(t_ff_24_q), .reset(and_27_out));  // open: Qn, preset, en
  Clock clock_1 (.out(clock_1_out));
  _7_Segment_Display u_7_segment_display_6 (
    .g(decoder_6_a0), .f(decoder_6_a1), .a(decoder_6_a2), .b(decoder_6_a3), .e(decoder_6_a4),
    .d(decoder_6_a5), .c(decoder_6_a6));  // open: dp
  decoder decoder_6 (
    .a(t_ff_24_q), .b(t_ff_23_q), .c(t_ff_22_q), .d(t_ff_21_q), .a0(decoder_6_a0), .a1(decoder_6_a1),
    .a2(decoder_6_a2), .a3(decoder_6_a3), .a4(decoder_6_a4), .a5(decoder_6_a5), .a6(decoder_6_a6));
  and and_27 (and_27_out, t_ff_22_q, t_ff_24_q);
  _7_Segment_Display u_7_segment_display_7 (.g(1'b1), .f(1'b1), .b(1'b1), .e(1'b1), .c(1'b1));  // open: a, d, dp
  _7_Segment_Display u_7_segment_display_8 (.f(1'b1), .a(1'b1), .e(1'b1));  // open: g, b, d, c, dp

  // Notes on the sheet:
  //   HOURS
  //   DIGITAL CLOCK DESIGN-24 HRS  FORMAT
  //   MINUTES
  //   SECONDS
endmodule

module decoder (
  input  a,
  input  b,
  input  c,
  input  d,
  output a0,
  output a1,
  output a2,
  output a3,
  output a4,
  output a5,
  output a6
);

  wire and_1_out, and_2_out, and_3_out, and_4_out, and_5_out, and_6_out, and_7_out, and_8_out, and_9_out,
       and_10_out, and_11_out, and_12_out, and_13_out, and_14_out, and_15_out, and_16_out, not_1_out,
       not_2_out, not_3_out, not_4_out, not_5_out, not_6_out, not_7_out, not_8_out, not_9_out, not_10_out,
       not_11_out, not_12_out, not_13_out, not_14_out, not_15_out, not_16_out, not_17_out, not_18_out,
       not_19_out, not_20_out, not_21_out;

  not not_1 (not_1_out, b);
  and and_1 (and_1_out, not_1_out, c);
  and and_2 (and_2_out, b, not_2_out);
  not not_2 (not_2_out, c);
  and and_3 (and_3_out, b, not_3_out);
  not not_3 (not_3_out, d);
  not not_4 (not_4_out, c);
  and and_4 (and_4_out, not_4_out, not_5_out);
  not not_5 (not_5_out, d);
  and and_5 (and_5_out, b, not_6_out);
  not not_6 (not_6_out, c);
  and and_6 (and_6_out, b, not_7_out);
  not not_7 (not_7_out, d);
  not not_8 (not_8_out, b);
  and and_7 (and_7_out, not_8_out, not_9_out);
  not not_9 (not_9_out, d);
  and and_8 (and_8_out, b, d);
  not not_10 (not_10_out, b);
  not not_11 (not_11_out, c);
  and and_9 (and_9_out, not_11_out, not_12_out);
  not not_12 (not_12_out, d);
  and and_10 (and_10_out, c, d);
  not not_13 (not_13_out, b);
  and and_11 (and_11_out, not_13_out, not_14_out);
  not not_14 (not_14_out, d);
  and and_12 (and_12_out, c, not_15_out);
  not not_15 (not_15_out, d);
  not not_16 (not_16_out, b);
  and and_13 (and_13_out, not_16_out, not_17_out);
  not not_17 (not_17_out, d);
  not not_18 (not_18_out, b);
  and and_14 (and_14_out, not_18_out, c);
  and and_15 (and_15_out, c, not_19_out);
  not not_19 (not_19_out, d);
  and and_16 (and_16_out, b, not_20_out, d);
  not not_20 (not_20_out, c);
  not not_21 (not_21_out, c);
  or or_1 (a6, not_21_out, d, b);
  or or_2 (a0, and_1_out, and_2_out, and_3_out, a);
  or or_3 (a1, and_4_out, and_5_out, and_6_out, a);
  or or_4 (a2, and_7_out, c, and_8_out, a);
  or or_5 (a3, not_10_out, and_9_out, and_10_out);
  or or_6 (a4, and_11_out, and_12_out);
  or or_7 (a5, and_13_out, and_14_out, and_15_out, and_16_out, a);
endmodule
